# Fritzing sketch Automated Cereal Dispenser (saved by Fritzing 0.9.3b)
breadboards: 1

parts:
  Cereal_Dispenser_Servo = Basic Servo
  Arduino_Power_Plug = Power plug
  Servo_Power_Plug = Power plug
  Arduino = Arduino Uno (Rev3)

nets:
  GND: Cereal_Dispenser_Servo.gnd, Arduino_Power_Plug.GND, Servo_Power_Plug.GND, Arduino.GND
  VCC: Cereal_Dispenser_Servo.vcc, Servo_Power_Plug.VCC
  N1: Cereal_Dispenser_Servo.pulse, Arduino.D6_PWM
  VCC_2: Arduino_Power_Plug.VCC, Arduino.5V
